# Fritzing sketch circuit (saved by Fritzing 0.9.3b)
breadboards: 1

parts:
  Part1 = Arduino Pro Mini (5V)  # not connected
  IC1 = Dual Op-Amp [package=dip08]
  R1 = Photocell (LDR) [package=THT]
  R2 = TRIMPOT [package=trim_pot_pth]
  R3 = Resistor [tolerance=±5% resistance=47k package=THT]
  SP1 = SPEAKER [package=pcb_mount_speaker]
  R10 = Resistor [tolerance=±5% resistance=4.7k package=THT]
  R11 = Resistor [tolerance=±5% resistance=2.2k package=THT]
  R13 = Resistor [tolerance=±5% resistance=4.7k package=THT]
  R14 = Resistor [tolerance=±5% resistance=2.2k package=THT]
  R15 = Resistor [tolerance=±5% resistance=2.2k package=THT]
  R16 = Resistor [tolerance=±5% resistance=4.7k package=THT]
  IC3 = Winbond [package=THT]
  R18 = Resistor [tolerance=±5% resistance=47k package=THT]
  C6 = Ceramic Capacitor [capacitance=100nF package="100 mil [THT, multilayer]"]
  IC5 = Voltage Regulator [package=to-92]
  Part2 = Adafruit Stereo 2.1W Class D Audio Amplifier - TPA2012 [part_number="Adafruit #1552"]
  C8 = Ceramic Capacitor [capacitance=100nF package="100 mil [THT, multilayer]"]
  C7 = Ceramic Capacitor [capacitance=100nF package="100 mil [THT, multilayer]"]

nets:
  N1: IC1.A_-IN, R1.pin_0, R3.Pin_0
  GND: IC1.A_V-, R1.pin_1, R2.CW, R10.Pin_0, R13.Pin_0, R16.Pin_0, IC3.GND, C6.0, IC5.GND, Part2.GND, Part2.IN_LEFT-, C8.0, C7.1
  N2: IC1.A_V+, R2.CCW, R3.Pin_1, C6.1, IC5.IN, Part2.VDD
  N3: SP1.+, Part2.OUT_LEFT-
  N4: SP1.-, Part2.OUT_LEFT+
  N5: R10.Pin_1, R11.Pin_0, IC3.SCL_-_I2C_Clock#5
  N6: R13.Pin_1, R15.Pin_0, IC3.MOSI#4
  N7: R14.Pin_0, R16.Pin_1, IC3.SCL_-_I2C_Clock#0, IC3.WP, R18.Pin_0
  N8: IC3.HOLD, IC3.VCC, R18.Pin_1, IC5.OUT, C8.1, C7.0

custom parts:
  Winbond: Winbond Serial Flash Memory
  Voltage Regulator: Voltage Regulator MCP1700 3.3V regulator. IGO (Input Ground Output)
  Adafruit Stereo 2.1W Class D Audio Amplifier - TPA2012: This incredibly small stereo amplifier is surprisingly powerful - able to deliver 2 x 2.1W channels into 4 ohm impedance speakers (@ 10% THD). Inside the miniature chip is a class D controller, able to run from 2.7V-5.5VDC. Since the amp is a class D, it's incredibly efficient (89% efficient when driving an 8Ω speaker at 1.5 Watt) - making it perfect for portable and battery-powered projects.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
